# Fritzing sketch NeoClock (saved by Fritzing 0.9.3b)
breadboards: 1

parts:
  Part1 = Arduino Pro Mini v13
  Part2 = DeadOn RTC - DS3234 Breakout
  U1 = Voltage Regulator - 5V [package="TO220 [THT]"]
  J1 = Power Jack [package=power_jack_slot]
  C1 = Capacitor Polarized [package=cpol-radial-1000uf-63v]
  Part3 = Quarter 60 NeoPixel Ring [part_number=1768]
  Part4 = Quarter 60 NeoPixel Ring [part_number=1768]
  Part5 = Quarter 60 NeoPixel Ring [part_number=1768]
  Part6 = Quarter 60 NeoPixel Ring [part_number=1768]
  Part7 = 24 NeoPixel Ring [part_number=1586]
  R1 = Resistor [tolerance=±5% resistance=470 package="2010 [SMD]"]
  R2 = Resistor [tolerance=±5% resistance=2.21 package="2010 [SMD]"]
  R7 = Resistor [tolerance=±5% resistance=2.21 package="1206 [SMD]"]
  S1 = SWITCH-MOMENTARY-2 [package=tactile-pth-12mm]
  S2 = SWITCH-MOMENTARY-2 [package=tactile-pth-12mm]

nets:
  VCC: Part1.VCC, Part2.VCC, S1.2, S2.2
  VDD: Part1.RAW, U1.output_voltage, C1.+, Part3.VDD, Part4.VDD, Part5.VDD, Part6.VDD, Part7.VDD
  GND: Part1.GND, Part2.INT/SQW, Part2.GND, U1.GND, J1.GNDBREAK, C1.-, Part3.GND, Part4.GND, Part5.GND, Part6.GND, Part7.GND, R2.Pin_1, R7.Pin_1
  N1: Part1.D13/SCK, Part2.SCLK
  N2: Part1.D12/MISO, Part2.MISO
  N3: Part1.D11_PWM/MOSI, Part2.MOSI
  N4: Part1.D10_PWM/SS, Part2.SS
  N5: Part1.D6_PWM, Part7.IN
  N6: Part1.D3_PWM, R7.Pin_0, S2.1
  N7: Part1.D2, R2.Pin_0, S1.1
  N8: U1.input_voltage, J1.PWR
  N9: Part3.DATAIN, Part4.DATAOUT
  N10: Part3.DATAOUT, Part6.DATAIN
  N11: Part4.DATAIN, R1.Pin_0
  N12: Part5.DATAIN, Part6.DATAOUT
  N13: Part7.OUT, R1.Pin_1

custom parts:
  Quarter 60 NeoPixel Ring: The biggest NeoPixel Ring yet! With four of these you can make a huge ring with 60 ultra bright smart LED NeoPixels are arranged in a circle with a 6.2" diameter. The rings are 'chainable' - connect the output pin of one to the input pin of another. Use only one microcontroller pin to control as many as you can chain together!
  24 NeoPixel Ring: 24 ultra bright smart LED NeoPixels are arranged in a circle with 2.6" (66mm) outer diameter. The rings are 'chainable' - connect the output pin of one to the input pin of another. Use only one microcontroller pin to control as many as you can chain together! Each LED is addressable as the driver chip is inside the LED. Each one has ~18mA constant current drive so the color will be very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
